# Fritzing sketch BlueRCCar (saved by Fritzing 0.9.3b)
stripboards: 1

parts:
  U1 = attiny85 [package=dip]
  BT1 = Bluetooth HC-06u [package=THT]
  R1 = Resistor [tolerance=±5% resistance=10k package=THT]
  VCC_5V = Header 1 [package=1x01_offset]
  GND = Header 1 [package=1x01_offset]
  EN = Header 1 [package=1x01_offset]
  U2_VCC = Header 1 [package=1x01_offset]
  U2_GND = Header 1 [package=1x01_offset]
  U2_SDA = Header 1 [package=1x01_offset]
  U2_SCL = Header 1 [package=1x01_offset]
  R2 = Resistor [tolerance=±5% resistance=1k package=THT]
  R3 = Resistor [tolerance=±5% resistance=2.2k package=THT]

nets:
  N1: U1.Pin_1, R1.Pin_0
  N2: U1.Pin_2, R2.Pin_1
  N3: U1.Pin_3, BT1.TXD
  N4: U1.Pin_4, BT1.GND, GND.1, U2_GND.1, R3.Pin_0
  N5: U1.Pin_5, U2_SDA.1
  N6: U1.Pin_6, EN.1
  N7: U1.Pin_7, U2_SCL.1
  N8: U1.Pin_8, BT1.VCC, R1.Pin_1, VCC_5V.1, U2_VCC.1
  N9: BT1.RXD, R2.Pin_0, R3.Pin_1

notes:
  U2 : PCF8574

custom parts:
  Bluetooth HC-06u: Bluetooth HC-06 - face up, pins down 16.5mm x 37.5mm PCB
